# Fritzing sketch UNUBLE (saved by Fritzing 0.9.0b)
breadboards: 1

parts:
  NANO = Arduino Nano (Rev3.0)
  UNU_BLE = Header 8 [package=1x08_smd]
  LED1 = RGB LED (com. cathode, rgb) [package="5 mm [THT]"]
  D1 = LTE-302 [package=lte-302]

nets:
  N1: NANO.GND, UNU_BLE.2, LED1.common_cathode, D1.C
  N2: NANO.D6, D1.A
  N3: NANO.D7, UNU_BLE.3
  N4: NANO.D8, UNU_BLE.4
  N5: NANO.3V3, UNU_BLE.1
  N6: UNU_BLE.5, LED1.blue_anode
  N7: UNU_BLE.6, LED1.green_anode
  N8: UNU_BLE.7, LED1.red_anode

notes:
  3V3
  GND
  TX
  RX
  PIO3
  PIO2
  LED
